# Fritzing sketch piezo_buzzer (saved by Fritzing 0.9.2b)
breadboards: 1

parts:
  Raspberry_Pi_B_rev2 = Raspberry Pi B rev2
  J1 = Piezo Speaker

nets:
  N1: Raspberry_Pi_B_rev2.GND, J1.pin1
  N2: Raspberry_Pi_B_rev2.GPIO_24, J1.pin2
