# Fritzing sketch single_LED (saved by Fritzing 0.9.2b)
breadboards: 1

parts:
  R1 = Resistor [tolerance=±5% resistance=220 package=THT]
  LED1 = smd LED [color="Red (635nm)" package="1206 [SMD]"]
  Raspberry_Pi_B_rev2 = Raspberry Pi B rev2

nets:
  N1: R1.Pin_0, R1.Pin_1, LED1.anode, Raspberry_Pi_B_rev2.GPIO_4
  N2: LED1.cathode, Raspberry_Pi_B_rev2.GND
