# Fritzing sketch ultrasonic_rangefinder (saved by Fritzing 0.9.2b)
breadboards: 1

parts:
  Raspberry_Pi_B_rev2 = Raspberry Pi B rev2
  Part1 = SRF05 Ultrasonic Rangefinder
  R1 = Resistor [tolerance=±5% resistance=1k package="0603 [SMD]"]
  R2 = Resistor [tolerance=±5% resistance=2k package="0603 [SMD]"]

nets:
  5V: Raspberry_Pi_B_rev2.5V, Part1.VCC
  N1: Raspberry_Pi_B_rev2.GPIO_27, Part1.Trig
  N2: Raspberry_Pi_B_rev2.GPIO_22, R1.Pin_1, R2.Pin_0
  GND: Raspberry_Pi_B_rev2.GND, Part1.GND, R2.Pin_1
  N3: Part1.Echo, R1.Pin_0
