# Fritzing sketch traffic_light_LEDs (saved by Fritzing 0.9.2b)
breadboards: 1

parts:
  R1 = Resistor [tolerance=±5% resistance=220 package=THT]
  LED1 = smd LED [color="Red (635nm)" package="1206 [SMD]"]
  S1 = Pushbutton [package="[THT]"]
  LED2 = smd LED [color="Orange (605nm)" package="1206 [SMD]"]
  LED3 = smd LED [color="Green (565nm)" package="1206 [SMD]"]
  R2 = Resistor [tolerance=±5% resistance=220 package=THT]
  R3 = Resistor [tolerance=±5% resistance=220 package=THT]
  Raspberry_Pi_B_rev2 = Raspberry Pi B rev2

nets:
  N1: R1.Pin_0, R1.Pin_1, LED1.anode, Raspberry_Pi_B_rev2.GPIO_4
  N2: LED1.cathode, S1.Pin_3, S1.Pin_4, LED2.cathode, LED3.cathode, Raspberry_Pi_B_rev2.GND
  N3: S1.Pin_1, S1.Pin_2, Raspberry_Pi_B_rev2.GPIO_25
  N4: LED2.anode, R2.Pin_0
  N5: LED3.anode, R3.Pin_0
  N6: R2.Pin_1, Raspberry_Pi_B_rev2.GPIO_17
  N7: R3.Pin_1, Raspberry_Pi_B_rev2.GPIO_23
